// Logisim project alarme_cinto.circ as structural Verilog
module alarme_cinto (
  input  s,
  input  ch,
  input  p,
  output alarme
);

  wire not_1_out, not_2_out;

  not not_1 (not_1_out, s);
  not not_2 (not_2_out, p);
  and and_1 (alarme, not_1_out, ch, not_2_out);
endmodule
