// Logisim project alarme_cinto_placa.circ as structural Verilog: 1 circuit, main circuit main
module main (
  input  S__Cinto,
  input  P_Pessioa,
  input  Ch__Chave,
  output out_4
);

  wire n7404_1_p2, n7404_1_p4, n7408_1_p3;

  // _7404 7404_1: pin names not known; wires that end beside it: S__Cinto, n7404_1_p2, P_Pessioa, n7404_1_p4
  // _7408 7408_1: pin names not known; wires that end beside it: n7404_1_p2, n7404_1_p4, n7408_1_p3, n7408_1_p3, Ch__Chave, out_4
endmodule
