// Logisim project calculadora_agora_vai.circ as structural Verilog: 1 circuit, main circuit main
module main (
  input  Soma,
  input  Multi,
  input  \Divisão ,
  input  Sub,
  input  [7:0] \Número_01 ,
  input  [7:0] \Número_02 
);

  wire and_2_out, and_3_out, and_4_out, and_5_out, and_6_out, and_out, clock_1_out, clock_2_out, clock_3_out,
       clock_4_out, comparator_1_gt, comparator_2_gt;
  wire [7:0] adder_1_out, divider_1_out, multiplier_1_out, register_1_q, register_2_q, register_4_q,
       register_5_q, register_8_q, register_9_q, register_11_q, register_12_q, subtractor_1_out;

  Register register_1 (.D(\Número_01 ), .Q(register_1_q), .clk(and_out));  // open: en, clr
  Register register_2 (.D(\Número_02 ), .Q(register_2_q), .clk(and_out));  // open: en, clr
  and \and  (and_out, Soma, ~Multi, ~\Divisão , ~Sub);  // AND_Gate
  Adder adder_1 (.a(register_1_q), .b(register_2_q), .out(adder_1_out));  // open: cin, cout
  Register register_3 (.D(adder_1_out), .clk(clock_1_out));  // open: en, Q, clr
  Clock clock_1 (.out(clock_1_out));
  Register register_4 (.D(\Número_01 ), .Q(register_4_q), .clk(and_2_out));  // open: en, clr
  Register register_5 (.D(\Número_02 ), .Q(register_5_q), .clk(and_2_out));  // open: en, clr
  and and_2 (and_2_out, ~Soma, Multi, ~\Divisão , ~Sub);  // AND_Gate
  Register register_6 (.D(multiplier_1_out), .clk(clock_2_out));  // open: en, Q, clr
  Clock clock_2 (.out(clock_2_out));
  Multiplier multiplier_1 (.a(register_4_q), .b(register_5_q), .out(multiplier_1_out));  // open: cin, cout
  Comparator comparator_1 (.a(\Número_01 ), .b(\Número_02 ), .gt(comparator_1_gt));  // open: eq, lt
  and and_3 (and_3_out, ~Soma, ~Multi, \Divisão , ~Sub);  // AND_Gate
  and and_4 (and_4_out, and_3_out, comparator_1_gt);
  Register register_7 (.D(divider_1_out), .clk(clock_3_out));  // open: en, Q, clr
  Clock clock_3 (.out(clock_3_out));
  Register register_8 (.D(\Número_01 ), .Q(register_8_q), .clk(and_4_out));  // open: en, clr
  Register register_9 (.D(\Número_02 ), .Q(register_9_q), .clk(and_4_out));  // open: en, clr
  and and_5 (and_5_out, ~Soma, ~Multi, ~\Divisão , Sub);  // AND_Gate
  Divider divider_1 (.a(register_8_q), .b(register_9_q), .out(divider_1_out));  // open: upper, rem
  Comparator comparator_2 (.a(\Número_01 ), .b(\Número_02 ), .gt(comparator_2_gt));  // open: eq, lt
  and and_6 (and_6_out, and_5_out, comparator_2_gt);
  Register register_10 (.D(subtractor_1_out), .clk(clock_4_out));  // open: en, Q, clr
  Clock clock_4 (.out(clock_4_out));
  Register register_11 (.D(\Número_01 ), .Q(register_11_q), .clk(and_6_out));  // open: en, clr
  Register register_12 (.D(\Número_02 ), .Q(register_12_q), .clk(and_6_out));  // open: en, clr
  Subtractor subtractor_1 (.a(register_11_q), .b(register_12_q), .out(subtractor_1_out));  // open: bin, bout
endmodule
