// Logisim project refri.circ as structural Verilog: 1 circuit, main circuit main
module main (
  input  C,
  input  [7:0] S,
  input  [7:0] a,
  output d
);

  wire and_2_out, and_3_out, and_4_out, and_5_out, and_6_out, clock_1_out, comparator_1_eq, comparator_1_gt,
       or_1_out, or_2_out, or_3_out, register_1_q, register_2_q;
  wire [7:0] adder_1_out, register_3_q;

  Register #(.width(1)) register_1 (.D(or_1_out), .Q(register_1_q), .clk(clock_1_out));  // open: en, clr
  Clock clock_1 (.out(clock_1_out));
  Register #(.width(1)) register_2 (.D(or_2_out), .Q(register_2_q), .clk(clock_1_out));  // open: en, clr
  and and_1 (d, register_1_q, register_2_q);
  and and_2 (and_2_out, register_1_q, ~register_2_q);  // AND_Gate
  and and_3 (and_3_out, ~register_1_q, ~register_2_q);  // AND_Gate
  and and_4 (and_4_out, ~register_1_q, register_2_q, or_3_out, ~C);  // AND_Gate
  and and_5 (and_5_out, ~register_1_q, register_2_q, C);  // AND_Gate
  and and_6 (and_6_out, ~register_1_q, register_2_q, ~C);  // AND_Gate
  or or_1 (or_1_out, and_4_out, and_5_out);
  or or_2 (or_2_out, ~register_2_q, and_6_out);  // OR_Gate
  Comparator comparator_1 (.a(register_3_q), .b(S), .gt(comparator_1_gt), .eq(comparator_1_eq));  // open: lt
  or or_3 (or_3_out, comparator_1_eq, comparator_1_gt);
  Register register_3 (.D(adder_1_out), .Q(register_3_q), .clk(and_2_out), .clr(and_3_out));  // open: en
  Adder adder_1 (.a(a), .b(register_3_q), .out(adder_1_out));  // open: cin, cout

  // Notes on the sheet:
  //   tot_lt_S
  //   S1
  //   S0
  //   tot_ld
  //   tot_clr
  //   tot_lt_s
endmodule
